# Fritzing sketch self-balance (saved by Fritzing 0.9.6b)
breadboards: 1

parts:
  Part2 = InvenSense MPU6050
  H-bridge = L298 [package=multiwatt15]
  Receiver = IC, SIP package, 8 pins [chip_label=RX]
  Motor_1 = DC Motor
  Motor_2 = DC Motor
  2S_LIPO = DC Power [voltage=8.4V]
  Part1 = Arduino Nano (Rev3.0) (ICSP)

nets:
  VCC: Part2.VCC, H-bridge.ENA, H-bridge.VLS, H-bridge.ENB, Receiver.pin7, Part1.5V
  GND: Part2.GND, H-bridge.GND, Receiver.pin8, 2S_LIPO.V-, Part1.GND
  N1: Part2.SCL, Part1.A5
  N2: Part2.SDA, Part1.A4
  N3: H-bridge.OUT1, Motor_1.pin_1
  N4: H-bridge.OUT2, Motor_1.pin_2
  N5: H-bridge.VS, 2S_LIPO.V+, Part1.VIN
  N6: H-bridge.IN1, Part1.D10
  N7: H-bridge.IN2, Part1.D9
  N8: H-bridge.IN3, Part1.D6
  N9: H-bridge.IN4, Part1.D5
  N10: H-bridge.OUT3, Motor_2.pin_1
  N11: H-bridge.OUT4, Motor_2.pin_2
  N12: Receiver.pin1, Part1.D2
  N13: Receiver.pin2, Part1.D3
